# Fritzing sketch psucontrol (saved by Fritzing 0.9.3b)

parts:
  KY-1 = Keyes Relay [package=THT]
  Raspberry_Pi1 = Raspberry Pi B+
  part = Resistor [tolerance=±5% resistance=1k package="2512 [SMD]"]
  NPN = NPN-Transistor [part_number=2N2222 package="TO92 [THT]"]

nets:
  N1: KY-1.signal, Raspberry_Pi1.5V
  N2: KY-1.power, Raspberry_Pi1.GND, NPN.C
  N3: KY-1.ground, NPN.E
  N4: Raspberry_Pi1.GPIO2, part.Pin_0
  N5: part.Pin_1, NPN.B

notes:
  Live
  Neutral
  Ground

custom parts:
  Keyes Relay: The Keyes 5V relay module is suitable for SCM development, home appliance control. It uses a 5V~12V TIL control signal which can control DC / AC signal.
